# Fritzing sketch oled (saved by Fritzing 0.9.4)

parts:
  ArduinoNano = Arduino Nano (Rev3.0)
  OLED = OLED 128x64 I2C Monochrome Display

nets:
  GND: ArduinoNano.GND, OLED.GND
  5V: ArduinoNano.5V, OLED.VDD
  N1: ArduinoNano.A5, OLED.SCK
  N2: ArduinoNano.A4, OLED.SDA
