# Fritzing sketch L298_Driver_Motor_Module (saved by Fritzing 0.9.4)

parts:
  Part2 = Arduino Nano (Rev3.0)
  M3 = DC Motor
  M4 = DC Motor
  VCC3 = 4 x AAA Battery Mount
  Mod1 = L298N DC motor driver

nets:
  N1: Part2.D7, Mod1.IN4
  N2: Part2.D8, Mod1.IN3
  N3: Part2.D9, Mod1.ENB
  N4: Part2.D10, Mod1.ENA
  N5: Part2.D11/MOSI, Mod1.IN2
  N6: Part2.D12/MISO, Mod1.IN1
  GND: Part2.GND, VCC3.-, Mod1.GND
  N7: M3.pin_1, Mod1.OUT4
  N8: M3.pin_2, Mod1.OUT3
  N9: M4.pin_1, Mod1.OUT2
  N10: M4.pin_2, Mod1.OUT1
  N11: VCC3.+, Mod1.12V

custom parts:
  L298N DC motor driver: 2x DC motor driver with 78M05 positive voltage regulator (7..35 V) L298N: max 46 V, 2 A Set 5 V Enable jumper to enable 5 V regultor (needed for the L298N) and +5 V output at screw terminal or supply external +5 V at screw terminal Set ENA and/or ENB to +5 V to enable motor permanently or supply ENA and/or ENB with PWM signal IN1 and IN2 set rotation directory for motor A (OUT1/OUT2) IN2 and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
