# Fritzing sketch Potentiometer (saved by Fritzing 0.9.4)
breadboards: 1

parts:
  U1 = POT [package=pot_alpha_rv16af-20]
  Part1 = Arduino Nano (Rev3.0)

nets:
  N1: U1.A, Part1.GND
  N2: U1.S, Part1.A0
  N3: U1.E, Part1.5V
