# Fritzing sketch Servo (saved by Fritzing 0.9.4)
breadboards: 1

parts:
  Part1 = Arduino Nano (Rev3.0)
  J1 = Basic Servo
  U1 = Voltage Regulator - 5V [package="DPak [SMD]"]  # not connected
  VCC1 = Battery block 9V

nets:
  N1: Part1.D5, J1.pulse
  N2: J1.gnd, VCC1.-
